// Logisim project CPU_Final.circ as structural Verilog
module One_Bit_Adder (
  input  A,
  input  B,
  input  Cin,
  output Q,
  output Carry_out
);

  wire nand_1_out, nand_2_out, nand_3_out, nand_5_out, nand_6_out, nand_7_out, nand_9_out, not_1_out,
       not_2_out, not_3_out;

  not not_1 (not_1_out, A);
  not not_2 (not_2_out, B);
  not not_3 (not_3_out, Cin);
  nand nand_1 (nand_1_out, not_1_out, not_2_out, Cin);
  nand nand_2 (nand_2_out, not_1_out, B, not_3_out);
  nand nand_3 (nand_3_out, A, B, Cin);
  nand nand_4 (Q, nand_1_out, nand_2_out, nand_3_out, nand_5_out);
  nand nand_5 (nand_5_out, A, not_2_out, not_3_out);
  nand nand_6 (nand_6_out, A, B);
  nand nand_7 (nand_7_out, B, Cin);
  nand nand_8 (Carry_out, nand_6_out, nand_7_out, nand_9_out);
  nand nand_9 (nand_9_out, A, Cin);
endmodule

module Eight_bit_Adder (
  input  [7:0] A,
  input  [7:0] B,
  input  Carry_in,
  output Carry_out,
  output [7:0] Q,
  output V_Overflow
);

  wire one_bit_adder_2_carry_out, one_bit_adder_3_carry_out, one_bit_adder_4_carry_out,
       one_bit_adder_5_carry_out, one_bit_adder_6_carry_out, one_bit_adder_7_carry_out,
       one_bit_adder_8_carry_out;

  xor xor_1 (V_Overflow, Carry_out, one_bit_adder_2_carry_out);
  One_Bit_Adder one_bit_adder_1 (.A(A[7]), .B(B[7]), .Cin(one_bit_adder_2_carry_out), .Q(Q[7]), .Carry_out(Carry_out));
  One_Bit_Adder one_bit_adder_2 (
    .A(A[6]), .B(B[6]), .Cin(one_bit_adder_3_carry_out), .Q(Q[6]), .Carry_out(one_bit_adder_2_carry_out));
  One_Bit_Adder one_bit_adder_3 (
    .A(A[5]), .B(B[5]), .Cin(one_bit_adder_4_carry_out), .Q(Q[5]), .Carry_out(one_bit_adder_3_carry_out));
  One_Bit_Adder one_bit_adder_4 (
    .A(A[4]), .B(B[4]), .Cin(one_bit_adder_5_carry_out), .Q(Q[4]), .Carry_out(one_bit_adder_4_carry_out));
  One_Bit_Adder one_bit_adder_5 (
    .A(A[3]), .B(B[3]), .Cin(one_bit_adder_6_carry_out), .Q(Q[3]), .Carry_out(one_bit_adder_5_carry_out));
  One_Bit_Adder one_bit_adder_6 (
    .A(A[2]), .B(B[2]), .Cin(one_bit_adder_7_carry_out), .Q(Q[2]), .Carry_out(one_bit_adder_6_carry_out));
  One_Bit_Adder one_bit_adder_7 (
    .A(A[1]), .B(B[1]), .Cin(one_bit_adder_8_carry_out), .Q(Q[1]), .Carry_out(one_bit_adder_7_carry_out));
  One_Bit_Adder one_bit_adder_8 (.A(A[0]), .B(B[0]), .Cin(Carry_in), .Q(Q[0]), .Carry_out(one_bit_adder_8_carry_out));
endmodule

module ALU (
  input  [7:0] B,
  input  [7:0] A,
  input  [3:0] STATUS_REGISTER_IN_VNZC,
  input  [3:0] OP_SEL,
  output [3:0] SREG_OUT_VNZC,
  output [7:0] out_6
);

  wire arithmetic_unit_1_cout, arithmetic_unit_1_v, logicunit_1_out_5;
  wire [7:0] arithmetic_unit_1_q, logicunit_1_o;

  Arithmetic_Unit arithmetic_unit_1 (
    .SEL_OP(OP_SEL[2:0]), .A(A), .B(B), .Cin(STATUS_REGISTER_IN_VNZC[0]), .Cout(arithmetic_unit_1_cout),
    .V(arithmetic_unit_1_v), .Q(arithmetic_unit_1_q));
  Multiplexer #(.width(8)) multiplexer_1 (.in0(arithmetic_unit_1_q), .in1(logicunit_1_o), .out(out_6), .sel(OP_SEL[3]));
  LogicUnit logicunit_1 (
    .SEL_OP(OP_SEL[2:0]), .A(A), .B(B), .Cin(STATUS_REGISTER_IN_VNZC[0]), .out_5(logicunit_1_out_5),
    .O(logicunit_1_o));
  Multiplexer multiplexer_2 (
    .in0(arithmetic_unit_1_cout), .in1(logicunit_1_out_5), .out(SREG_OUT_VNZC[0]), .sel(OP_SEL[3]));
  nor nor_1 (SREG_OUT_VNZC[1], out_6[7], out_6[6], out_6[5], out_6[4], out_6[3], out_6[2], out_6[1], out_6[0]);
  Multiplexer multiplexer_3 (
    .in0(arithmetic_unit_1_v), .in1(STATUS_REGISTER_IN_VNZC[3]), .out(SREG_OUT_VNZC[3]), .sel(OP_SEL[3]));

  assign SREG_OUT_VNZC[2] = out_6[7];

  // Notes on the sheet:
  //   0000=ADD 0001=ADC 0010=INC 0011=DEC 0100=NEG 0101=SUB 0110=SBC 0111=MOV 1000=AND 1001=OR 1010=XOR 1011=NOT 1100=LSL 1101=LSR 1110=ROL 1111=ROR
endmodule

module LSL (
  input  [7:0] A,
  output Cout,
  output [7:0] O
);


  assign Cout = A[7];
  assign O = {A[6:0], 1'b0};
endmodule

module LSR (
  input  [7:0] A,
  output Cout,
  output [7:0] O
);


  assign Cout = A[0];
  assign O = {1'b0, A[7:1]};
endmodule

module LogicUnit (
  input  Cin,
  input  [7:0] A,
  input  [7:0] B,
  input  [2:0] SEL_OP,
  output out_5,
  output [7:0] O
);

  wire lsl_1_cout, lsr_1_cout, roll_1_cout, rorr_1_cout;
  wire [7:0] and_1_out, lsl_1_o, lsr_1_o, not_1_out, or_1_out, roll_1_o, rorr_1_o, xor_1_out;

  assign and_1_out = A & B;  // AND_Gate and_1, 8 bits wide
  assign or_1_out = A | B;  // OR_Gate or_1, 8 bits wide
  assign xor_1_out = A ^ B;  // XOR_Gate xor_1, 8 bits wide
  assign not_1_out = ~A;  // NOT_Gate not_1, 8 bits wide
  Multiplexer #(.select(3), .width(8)) multiplexer_1 (
    .in0(and_1_out), .in1(or_1_out), .in2(xor_1_out), .in3(not_1_out), .in4(lsl_1_o), .in5(lsr_1_o),
    .in6(roll_1_o), .in7(rorr_1_o), .out(O), .sel(SEL_OP));
  LSL lsl_1 (.A(A), .Cout(lsl_1_cout), .O(lsl_1_o));
  LSR lsr_1 (.A(A), .O(lsr_1_o), .Cout(lsr_1_cout));
  ROLL roll_1 (.A(A), .Cin(Cin), .Cout(roll_1_cout), .O(roll_1_o));
  Multiplexer #(.select(3)) multiplexer_2 (
    .in0(Cin), .in1(Cin), .in2(Cin), .in3(Cin), .in4(lsl_1_cout), .in5(lsr_1_cout), .in6(roll_1_cout),
    .in7(rorr_1_cout), .out(out_5), .sel(SEL_OP));
  RORR rorr_1 (.Cin(Cin), .A(A), .O(rorr_1_o), .Cout(rorr_1_cout));

  // Notes on the sheet:
  //   And
endmodule

module Arithmetic_Unit (
  input  [7:0] A,
  input  [7:0] B,
  input  Cin,
  input  [2:0] SEL_OP,
  output Cout,
  output [7:0] Q,
  output V
);

  wire multiplexer_3_out, not_3_out;
  wire [7:0] multiplexer_1_out, multiplexer_2_out, not_1_out, not_2_out;

  assign not_1_out = ~A;  // NOT_Gate not_1, 8 bits wide
  Multiplexer #(.select(3), .width(8)) multiplexer_1 (
    .in0(A), .in1(A), .in2(A), .in3(A), .in4(not_1_out), .in5(A), .in6(A), .in7({8{1'b0}}),
    .out(multiplexer_1_out), .sel(SEL_OP));
  assign not_2_out = ~B;  // NOT_Gate not_2, 8 bits wide
  Multiplexer #(.select(3), .width(8)) multiplexer_2 (
    .in0(B), .in1(B), .in2(8'h1), .in3({8{1'b1}}), .in4(8'h1), .in5(not_2_out), .in6(not_2_out), .in7(B),
    .out(multiplexer_2_out), .sel(SEL_OP));
  Eight_bit_Adder eight_bit_adder_1 (
    .B(multiplexer_2_out), .A(multiplexer_1_out), .Carry_in(multiplexer_3_out), .V_Overflow(V),
    .Carry_out(Cout), .Q(Q));
  not not_3 (not_3_out, Cin);
  Multiplexer #(.select(3)) multiplexer_3 (
    .in0(1'b0), .in1(Cin), .in2(1'b0), .in3(1'b0), .in4(1'b0), .in5(1'b1), .in6(not_3_out), .in7(1'b0),
    .out(multiplexer_3_out), .sel(SEL_OP));
endmodule

module GPR (
  input  [7:0] Data,
  input  [2:0] Addr,
  input  CLK,
  input  EN_REG,
  input  Reset,
  input  [2:0] SEL_Out1,
  input  [2:0] SEL_OUT2,
  output [7:0] Out1,
  output [7:0] Out2
);

  wire and_1_out, decoder_1_out0, decoder_1_out1, decoder_1_out2, decoder_1_out3, decoder_1_out4,
       decoder_1_out5, decoder_1_out6, decoder_1_out7;
  wire [7:0] R0_q, R1_q, R2_q, R3_q, R4_q, R5_q, R6_q, R7_q;

  Decoder #(.enable("false"), .select(3)) decoder_1 (
    .out0(decoder_1_out0), .out1(decoder_1_out1), .out2(decoder_1_out2), .out3(decoder_1_out3),
    .out4(decoder_1_out4), .out5(decoder_1_out5), .out6(decoder_1_out6), .out7(decoder_1_out7), .sel(Addr));
  and and_1 (and_1_out, CLK, EN_REG);
  Register R0 (.D(Data), .en(decoder_1_out0), .clk(and_1_out), .Q(R0_q), .clr(Reset));
  Register R4 (.D(Data), .en(decoder_1_out4), .clk(and_1_out), .Q(R4_q), .clr(Reset));
  Multiplexer #(.select(3), .width(8)) multiplexer_1 (
    .in0(R0_q), .in1(R1_q), .in2(R2_q), .in3(R3_q), .in4(R4_q), .in5(R5_q), .in6(R6_q), .in7(R7_q),
    .out(Out1), .sel(SEL_Out1));
  Register R1 (.D(Data), .en(decoder_1_out1), .clk(and_1_out), .Q(R1_q), .clr(Reset));
  Register R5 (.D(Data), .en(decoder_1_out5), .clk(and_1_out), .Q(R5_q), .clr(Reset));
  Register R2 (.D(Data), .en(decoder_1_out2), .clk(and_1_out), .Q(R2_q), .clr(Reset));
  Register R6 (.D(Data), .en(decoder_1_out6), .clk(and_1_out), .Q(R6_q), .clr(Reset));
  Register R3 (.D(Data), .en(decoder_1_out3), .clk(and_1_out), .Q(R3_q), .clr(Reset));
  Register R7 (.D(Data), .en(decoder_1_out7), .clk(and_1_out), .Q(R7_q), .clr(Reset));
  Multiplexer #(.select(3), .width(8)) multiplexer_2 (
    .in0(R0_q), .in1(R1_q), .in2(R2_q), .in3(R3_q), .in4(R4_q), .in5(R5_q), .in6(R6_q), .in7(R7_q),
    .out(Out2), .sel(SEL_OUT2));
endmodule

module CPU (
  input  [15:0] FLASH_DATA,
  input  [7:0] valueFromRAM,
  input  CLOCK,
  input  reset,
  output [3:0] adressRAM,
  output [7:0] DataToRam,
  output rEn_RAM,
  output wEn_RAM,
  output [7:0] Flash_Address
);

  wire id_1_en_jmp_br, id_1_flag_cmp, id_1_force_jmp, id_1_sreg_wen, id_1_wen_gpr, multiplexer_2_out,
       multiplexer_4_out, not_1_out, or_1_out, xnor_1_out;
  wire [1:0] id_1_flag_sel, id_1_gpr_ss;
  wire [2:0] id_1_reg_a, id_1_reg_b;
  wire [3:0] alu_1_sreg_out_vnzc, id_1_alu_sel_op, SREG_q;
  wire [7:0] adder_1_out, alu_1_out_6, gpr_1_out2, id_1_bot_8, multiplexer_1_out, multiplexer_3_out;
  wire [15:0] IR_q;

  ID id_1 (
    .Instruction(IR_q), .BOT_8(id_1_bot_8), .flag_sel(id_1_flag_sel), .flag_cmp(id_1_flag_cmp),
    .ALU_SEL_OP(id_1_alu_sel_op), .Reg_A(id_1_reg_a), .force_JMP(id_1_force_jmp), .rEN_RAM(rEn_RAM),
    .wEn_RAM(wEn_RAM), .en_JMP_BR(id_1_en_jmp_br), .sReg_wEn(id_1_sreg_wen), .wEn_GPR(id_1_wen_gpr),
    .GPR_SS(id_1_gpr_ss), .ADDRESS_RAM(adressRAM), .REG_B(id_1_reg_b));
  Register #(.width(16)) IR (.D(FLASH_DATA), .en(1'b1), .Q(IR_q), .clk(CLOCK));  // open: clr
  not not_1 (not_1_out, CLOCK);
  Adder adder_1 (.a(Flash_Address), .b(8'h1), .out(adder_1_out), .cin(1'b0));  // open: cout
  Multiplexer #(.disabled("Z"), .width(8)) multiplexer_1 (
    .in0(adder_1_out), .in1(id_1_bot_8), .out(multiplexer_1_out), .sel(multiplexer_2_out));
  Register PC (.D(multiplexer_1_out), .en(1'b1), .Q(Flash_Address), .clk(not_1_out), .clr(reset));
  Multiplexer multiplexer_2 (.in0(1'b0), .in1(or_1_out), .out(multiplexer_2_out), .sel(id_1_en_jmp_br));
  or or_1 (or_1_out, id_1_force_jmp, xnor_1_out);
  xnor xnor_1 (xnor_1_out, id_1_flag_cmp, multiplexer_4_out);
  GPR gpr_1 (
    .CLK(not_1_out), .EN_REG(id_1_wen_gpr), .Reset(reset), .Addr(id_1_reg_a), .SEL_Out1(id_1_reg_a),
    .SEL_OUT2(id_1_reg_b), .Data(multiplexer_3_out), .Out1(DataToRam), .Out2(gpr_1_out2));
  ALU alu_1 (
    .A(gpr_1_out2), .OP_SEL(id_1_alu_sel_op), .B(DataToRam), .STATUS_REGISTER_IN_VNZC(SREG_q),
    .out_6(alu_1_out_6), .SREG_OUT_VNZC(alu_1_sreg_out_vnzc));
  Multiplexer #(.select(2), .width(8)) multiplexer_3 (
    .in0(id_1_bot_8), .in1(valueFromRAM), .in2(alu_1_out_6), .in3({4'b0000, SREG_q}),
    .out(multiplexer_3_out), .sel(id_1_gpr_ss));
  Register #(.width(4)) SREG (.D(alu_1_sreg_out_vnzc), .en(id_1_sreg_wen), .Q(SREG_q), .clk(not_1_out), .clr(reset));
  Multiplexer #(.disabled("Z"), .select(2)) multiplexer_4 (
    .in0(SREG_q[0]), .in1(SREG_q[1]), .in2(SREG_q[2]), .in3(SREG_q[3]), .out(multiplexer_4_out),
    .sel(id_1_flag_sel));

  // Notes on the sheet:
  //   VNZC
endmodule

module ID (
  input  [15:0] Instruction,
  output [2:0] REG_B,
  output [3:0] ADDRESS_RAM,
  output [3:0] ALU_SEL_OP,
  output [7:0] BOT_8,
  output [1:0] flag_sel,
  output flag_cmp,
  output [2:0] Reg_A,
  output force_JMP,
  output rEN_RAM,
  output wEn_RAM,
  output en_JMP_BR,
  output sReg_wEn,
  output wEn_GPR,
  output [1:0] GPR_SS
);

  ROM #(.addrWidth(4)) rom_1 (
    .addr(Instruction[15:12]), .data({GPR_SS, wEn_GPR, sReg_wEn, en_JMP_BR, wEn_RAM, rEN_RAM, force_JMP}));

  assign ADDRESS_RAM = Instruction[3:0];
  assign ALU_SEL_OP = Instruction[7:4];
  assign BOT_8 = Instruction[7:0];
  assign flag_cmp = Instruction[10];
  assign flag_sel = Instruction[9:8];
  assign Reg_A = Instruction[10:8];
  assign REG_B = Instruction[2:0];

  // Notes on the sheet:
  //   contents of rom_1 (hex, n*v repeats v):
  //   b0 10 20 62 4 9 8
endmodule

module MPU (
);

  wire Clear_out, clock_1_out, cpu_1_ren_ram, cpu_1_wen_ram, not_1_out, RESET_out;
  wire [3:0] cpu_1_adressram;
  wire [7:0] cpu_1_datatoram, cpu_1_flash_address, ram_1_dout;
  wire [15:0] rom_1_data;

  ROM #(.dataWidth(16)) rom_1 (.addr(cpu_1_flash_address), .data(rom_1_data));
  CPU cpu_1 (
    .valueFromRAM(ram_1_dout), .CLOCK(clock_1_out), .FLASH_DATA(rom_1_data), .reset(RESET_out),
    .adressRAM(cpu_1_adressram), .rEn_RAM(cpu_1_ren_ram), .DataToRam(cpu_1_datatoram),
    .wEn_RAM(cpu_1_wen_ram), .Flash_Address(cpu_1_flash_address));
  Button RESET (.out(RESET_out));
  Clock clock_1 (.out(clock_1_out));
  not not_1 (not_1_out, clock_1_out);
  Button Clear (.out(Clear_out));
  RAM #(.addrWidth(4), .asyncread("true"), .clearpin("true")) ram_1 (
    .addr(cpu_1_adressram), .we(cpu_1_wen_ram), .oe(cpu_1_ren_ram), .clk(not_1_out), .din(cpu_1_datatoram),
    .dout(ram_1_dout), .clr(Clear_out));

  // Notes on the sheet:
  //   contents of rom_1 (hex, n*v repeats v):
  //   2502 571 30ab 170 c0 c0 1 40ab
endmodule

module ROLL (
  input  [7:0] A,
  input  Cin,
  output Cout,
  output [7:0] O
);


  assign Cout = A[7];
  assign O = {A[6:0], Cin};
endmodule

module RORR (
  input  [7:0] A,
  input  Cin,
  output Cout,
  output [7:0] O
);


  assign Cout = A[0];
  assign O = {Cin, A[7:1]};
endmodule
